// Logisim project computer.circ as structural Verilog
module cpu (
  input  in_1
);

  wire clk_1_clock_out, clock_1_out;
  wire [3:0] pull_resistor_4_node, pull_resistor_8_node, pull_resistor_12_node, pull_resistor_16_node;
  wire [15:0] program_counter_1_always_out;

  Clock clock_1 (.out(clock_1_out));
  CLK clk_1 (.CLOCK_IN(clock_1_out), .CLOCK_ENABLE(in_1), .CLOCK_OUT(clk_1_clock_out));  // open: MANUAL_TICK, HALT
  Hex_Digit_Display hex_digit_display_1 (.value(pull_resistor_4_node));  // open: dp
  LED led_1 (.in(pull_resistor_4_node[3]));
  LED led_2 (.in(pull_resistor_4_node[2]));
  LED led_3 (.in(pull_resistor_4_node[1]));
  Pull_Resistor pull_resistor_1 (.node(pull_resistor_4_node[3]));
  Pull_Resistor pull_resistor_2 (.node(pull_resistor_4_node[2]));
  Pull_Resistor pull_resistor_3 (.node(pull_resistor_4_node[1]));
  LED led_4 (.in(pull_resistor_4_node[0]));
  LED led_5 (.in(pull_resistor_8_node[3]));
  Pull_Resistor pull_resistor_4 (.node(pull_resistor_4_node[0]));
  Pull_Resistor pull_resistor_5 (.node(pull_resistor_8_node[3]));
  Hex_Digit_Display hex_digit_display_2 (.value(pull_resistor_8_node));  // open: dp
  LED led_6 (.in(pull_resistor_8_node[2]));
  LED led_7 (.in(pull_resistor_8_node[1]));
  LED led_8 (.in(pull_resistor_8_node[0]));
  Pull_Resistor pull_resistor_6 (.node(pull_resistor_8_node[2]));
  Pull_Resistor pull_resistor_7 (.node(pull_resistor_8_node[1]));
  Pull_Resistor pull_resistor_8 (.node(pull_resistor_8_node[0]));
  LED led_9 (.in(pull_resistor_12_node[3]));
  LED led_10 (.in(pull_resistor_12_node[2]));
  Pull_Resistor pull_resistor_9 (.node(pull_resistor_12_node[3]));
  Pull_Resistor pull_resistor_10 (.node(pull_resistor_12_node[2]));
  Hex_Digit_Display hex_digit_display_3 (.value(pull_resistor_12_node));  // open: dp
  LED led_11 (.in(pull_resistor_12_node[1]));
  LED led_12 (.in(pull_resistor_12_node[0]));
  Pull_Resistor pull_resistor_11 (.node(pull_resistor_12_node[1]));
  Pull_Resistor pull_resistor_12 (.node(pull_resistor_12_node[0]));
  Hex_Digit_Display hex_digit_display_4 (.value(pull_resistor_16_node));  // open: dp
  LED led_13 (.in(pull_resistor_16_node[3]));
  LED led_14 (.in(pull_resistor_16_node[2]));
  LED led_15 (.in(pull_resistor_16_node[1]));
  Pull_Resistor pull_resistor_13 (.node(pull_resistor_16_node[3]));
  Pull_Resistor pull_resistor_14 (.node(pull_resistor_16_node[2]));
  Pull_Resistor pull_resistor_15 (.node(pull_resistor_16_node[1]));
  LED led_16 (.in(pull_resistor_16_node[0]));
  Pull_Resistor pull_resistor_16 (.node(pull_resistor_16_node[0]));
  LED led_17 (.in(program_counter_1_always_out[15]));
  LED led_18 (.in(program_counter_1_always_out[14]));
  LED led_19 (.in(program_counter_1_always_out[13]));
  LED led_20 (.in(program_counter_1_always_out[12]));
  LED led_21 (.in(program_counter_1_always_out[11]));
  LED led_22 (.in(program_counter_1_always_out[10]));
  LED led_23 (.in(program_counter_1_always_out[9]));
  LED led_24 (.in(program_counter_1_always_out[8]));
  LED led_25 (.in(program_counter_1_always_out[7]));
  LED led_26 (.in(program_counter_1_always_out[6]));
  LED led_27 (.in(program_counter_1_always_out[5]));
  LED led_28 (.in(program_counter_1_always_out[4]));
  LED led_29 (.in(program_counter_1_always_out[3]));
  LED led_30 (.in(program_counter_1_always_out[2]));
  LED led_31 (.in(program_counter_1_always_out[1]));
  LED led_32 (.in(program_counter_1_always_out[0]));
  program_counter program_counter_1 (
    .CLOCK(clk_1_clock_out),
    .ADDRESS_IN({pull_resistor_4_node, pull_resistor_8_node, pull_resistor_12_node, pull_resistor_16_node}),
    .ALWAYS_OUT(program_counter_1_always_out),
    .ADDRESS_OUT({pull_resistor_4_node, pull_resistor_8_node, pull_resistor_12_node, pull_resistor_16_node}));  // open: COUNTER_OUT, RESET, JUMP, COUNTER_ENABLE

  // Notes on the sheet:
  //   ADDRESS BUS
endmodule

module CLK (
  input  CLOCK_IN,
  input  CLOCK_ENABLE,
  input  MANUAL_TICK,
  input  HALT,
  output CLOCK_OUT
);

  wire and_1_out, and_2_out, not_1_out, not_2_out, or_1_out;

  not not_1 (not_1_out, CLOCK_ENABLE);
  and and_1 (and_1_out, CLOCK_IN, CLOCK_ENABLE);
  and and_2 (and_2_out, not_1_out, MANUAL_TICK);
  or or_1 (or_1_out, and_1_out, and_2_out);
  not not_2 (not_2_out, HALT);
  and and_3 (CLOCK_OUT, or_1_out, not_2_out);
endmodule

module program_counter (
  input  RESET,
  input  JUMP,
  input  COUNTER_ENABLE,
  input  CLOCK,
  input  [15:0] ADDRESS_IN,
  input  COUNTER_OUT,
  output [15:0] ALWAYS_OUT,
  output [15:0] ADDRESS_OUT
);

  Counter #(.max('hffff), .width(16)) counter_1 (
    .clr(RESET), .load(JUMP), .up(COUNTER_ENABLE), .count(COUNTER_ENABLE), .clk(CLOCK), .D(ADDRESS_IN),
    .Q(ALWAYS_OUT));  // open: carry
  assign ADDRESS_OUT = COUNTER_OUT ? ALWAYS_OUT : 16'bz;  // Controlled_Buffer controlled_buffer_1
endmodule
